# Fritzing sketch LaserHarp (saved by Fritzing 0.9.3b)
breadboards: 3

parts:
  Part1 = PocketBeagle
  LED1 = smd LED [color="Red (633nm)" package="1206 [SMD]"]
  LED2 = smd LED [color="Red (633nm)" package="1206 [SMD]"]
  LED3 = smd LED [color="Red (633nm)" package="1206 [SMD]"]
  LED4 = smd LED [color="Red (633nm)" package="1206 [SMD]"]
  LED5 = smd LED [color="Red (633nm)" package="1206 [SMD]"]
  LED6 = smd LED [color="Red (633nm)" package="1206 [SMD]"]
  LED7 = smd LED [color="Red (633nm)" package="1206 [SMD]"]
  LED8 = smd LED [color="Red (633nm)" package="1206 [SMD]"]
  R1 = Resistor [tolerance=±5% resistance=2.2k package="0402 [SMD]"]
  R2 = Resistor [tolerance=±5% resistance=1k package="0402 [SMD]"]
  R3 = Photocell (LDR) [package=THT]
  R4 = Photocell (LDR) [package=THT]
  R5 = Photocell (LDR) [package=THT]
  R6 = Photocell (LDR) [package=THT]
  R7 = Photocell (LDR) [package=THT]
  R8 = Photocell (LDR) [package=THT]
  R9 = Photocell (LDR) [package=THT]
  R10 = Photocell (LDR) [package=THT]
  R11 = Resistor [tolerance=±5% resistance=10k package="0402 [SMD]"]
  R12 = Resistor [tolerance=±5% resistance=10k package="0402 [SMD]"]
  R13 = Resistor [tolerance=±5% resistance=10k package="0402 [SMD]"]
  R14 = Resistor [tolerance=±5% resistance=10k package="0402 [SMD]"]
  R15 = Resistor [tolerance=±5% resistance=10k package="0402 [SMD]"]
  R16 = Resistor [tolerance=±5% resistance=10k package="0402 [SMD]"]
  R17 = Resistor [tolerance=±5% resistance=10k package="0402 [SMD]"]
  R18 = Resistor [tolerance=±5% resistance=10k package="0402 [SMD]"]
  J1 = Piezo Speaker

nets:
  N1: Part1.3.3V, LED1.cathode, LED2.cathode, LED3.cathode, LED4.cathode, LED5.cathode, LED6.cathode, LED7.cathode, LED8.cathode, R1.Pin_0
  N2: Part1.GND, LED1.anode, LED2.anode, LED3.anode, LED4.anode, LED5.anode, LED6.anode, LED7.anode, LED8.anode, R2.Pin_0, R11.Pin_0, R12.Pin_0, R13.Pin_0, R14.Pin_0, R15.Pin_0, R16.Pin_0, R17.Pin_0, R18.Pin_0, J1.pin1
  N3: Part1.AIN0(1.8V), R3.pin_0, R18.Pin_1
  N4: Part1.AIN1(1.8V), R4.pin_0, R17.Pin_1
  N5: Part1.AIN2(1.8V), R5.pin_0, R16.Pin_1
  N6: Part1.AIN3(1.8V), R6.pin_0, R15.Pin_1
  N7: Part1.AIN4(1.8V), R7.pin_0, R14.Pin_1
  N8: R1.Pin_1, R2.Pin_1, R3.pin_1, R4.pin_1, R5.pin_1, R6.pin_1, R7.pin_1, R8.pin_1, R9.pin_1, R10.pin_1
  N9: R8.pin_0, R10.pin_0, R11.Pin_1, R13.Pin_1
  N10: R9.pin_0, R12.Pin_1

notes:
  STEMMA Speaker
  LDR Breadboard
  Laser Diode (5V 650nm 5mW) Breadboard
